# Fritzing sketch sensor_shield (saved by Fritzing 0.9.3b)
circuit board: 6.9215cm x 5.33756cm
breadboards: 1

parts:
  DGS = female pin header, 8 pins [form="♀ (female)"]
  V2_1 = Arduino Uno (Rev3)
  Fan = female pin header, 2 pins [form="♀ (female)"]
  1602A_(LCD) = female pin header, 16 pins [form="♀ (female)"]
  DS1307_(RTC) = female pin header, 5 pins [form="♀ (female)"]
  R1 = Trimmer Potentiometer [maximum_resistance=10kΩ package=THT]
  R2 = Resistor [tolerance=±5% resistance=1k package="2512 [SMD]"]
  RFM95W_(Radio) = female pin header, 9 pins [form="♀ (female)"]

nets:
  N1: DGS.pin2, V2_1.D8
  N2: DGS.pin3, V2_1.D7
  N3: DGS.pin6, V2_1.GND, Fan.pin1, 1602A_(LCD).pin1, 1602A_(LCD).pin5, 1602A_(LCD).pin16, DS1307_(RTC).pin1, R1.leg1, RFM95W_(Radio).pin2
  N4: DGS.pin8, V2_1.3V3
  N5: V2_1.A0, 1602A_(LCD).pin4
  N6: V2_1.A1, 1602A_(LCD).pin6
  N7: V2_1.A2, R2.Pin_0
  N8: V2_1.A3, 1602A_(LCD).pin14
  N9: V2_1.A4/SDA, DS1307_(RTC).pin3
  N10: V2_1.A5/SCL, DS1307_(RTC).pin5
  N11: V2_1.D9_PWM, 1602A_(LCD).pin11
  N12: V2_1.D10_PWM/SS, 1602A_(LCD).pin12
  N13: V2_1.D11_PWM/MOSI, RFM95W_(Radio).pin7
  N14: V2_1.D12/MISO, RFM95W_(Radio).pin6
  N15: V2_1.D13/SCK, RFM95W_(Radio).pin5
  N16: V2_1.D2, RFM95W_(Radio).pin9
  N17: V2_1.D3_PWM, RFM95W_(Radio).pin4
  N18: V2_1.D4, RFM95W_(Radio).pin8
  N19: V2_1.D5_PWM, 1602A_(LCD).pin13
  N20: V2_1.5V, Fan.pin2, 1602A_(LCD).pin2, DS1307_(RTC).pin2, RFM95W_(Radio).pin1
  N21: 1602A_(LCD).pin3, R1.wiper
  N22: 1602A_(LCD).pin15, R2.Pin_1
